// Digital circuit CPU.dig as structural Verilog
// The Radboud University Nijmegen Central Processing Unit (RUNCPU), which is a basic 32-bit CPU for the Processors course, part of the Computing Science Bachelor.
module CPU (
  input  Clock,
  input  [31:0] Databus_in,
  output [31:0] Addressbus,
  output [31:0] Databus_out,
  output nRE,
  output nWE,
  output Halted
);

  wire ALU_p4, ALU_p5, ALU_p6, FlagRegisterBank_carry_out, FlagRegisterBank_negative_out,
       FlagRegisterBank_overflow_out, FlagRegisterBank_zero_out, InstructionDecoder_p4,
       InstructionDecoder_p5, InstructionDecoder_p6, InstructionDecoder_p7, RegisterBank_p5, RegisterBank_p6,
       Timer_p2, Timer_p4, Timer_p5;
  wire [3:0] InstructionDecoder_p8;

  // Timer Timer: pin names not known; wires that end beside it: Clock, Timer_p2, Halted, Timer_p4, Timer_p5
  // InstructionDecoder InstructionDecoder: pin names not known; wires that end beside it: Databus_in, Timer_p4, Timer_p5, InstructionDecoder_p4, InstructionDecoder_p5, InstructionDecoder_p6, InstructionDecoder_p7, InstructionDecoder_p8, nRE, nWE
  // RegisterBank RegisterBank: pin names not known; wires that end beside it: InstructionDecoder_p4, InstructionDecoder_p5, InstructionDecoder_p6, Clock, RegisterBank_p5, RegisterBank_p6
  FlagRegisterBank FlagRegisterBank (
    .Carry_in(ALU_p6), .Overflow_in(ALU_p5), .Negative_in(ALU_p4), .Clock(Clock),
    .Carry_out(FlagRegisterBank_carry_out), .Overflow_out(FlagRegisterBank_overflow_out),
    .Negative_out(FlagRegisterBank_negative_out), .Zero_out(FlagRegisterBank_zero_out));  // open: Zero_in
  // ALU ALU: pin names not known; wires that end beside it: RegisterBank_p6, InstructionDecoder_p7, RegisterBank_p5, ALU_p4, ALU_p5, ALU_p6, Databus_out, Addressbus
  Tester Tester (
    .Condition(InstructionDecoder_p8), .Carry_in(FlagRegisterBank_carry_out),
    .Overflow_in(FlagRegisterBank_overflow_out), .Negative_in(FlagRegisterBank_negative_out),
    .Zero_in(FlagRegisterBank_zero_out), .TestSucceeds(Timer_p2));

  // Notes on the sheet:
  //   Addressbus: The addressbus signal, which determines the address of a read or write operation. For a write operation the address is where a value being written by the CPU should be stored. For a read operation the address is where a value being read by the CPU should be read from.
  //   Databus_out: The databus signal from the CPU. Any values written by the CPU will be stored here.
  //   nRE: Active low read enabled signal. When a read operation is performed by the CPU this value is set to low.
  //   nWE: Active low write enabled signal. When a write operation is performed by the CPU this value is set to low.
  //   Halted: Determines whether the CPU is in the halted state, in which it shall remain until the CPU is restarted.
  //   Databus_in: The databus signal to the CPU. Any values read (or instructions fetched) by the CPU will be stored here.
endmodule

/* Test case init:
Clock Databus_in Halted nRE nWE Databus_out Addressbus
0     0          0      0   1   x           0
*/

/* Test case add:
Clock Databus_in Halted nRE nWE Databus_out Addressbus R3
# The first line of test data must be the header, which contains the inputs and outputs used in the test case.
# It is possible to use registers in test cases by enabling their 'use as measurement value' attribute in the advanced tab.
# The R0-R15 registers have this attribute enabled in the provided template.

# These init statements are used to set the register contents when the simulation is started.
# Note that all init statements are collected and executed first. Interleaving them with regular test data has no effect.
# If you wish to test other instructions, or with different values, you must add a new test case component to the circuit.
# If you do not do this, the tests will run sequentially, meaning the next test will use the CPU state obtained after executing the prior test.
# This is reflected below in the last test data row that checks if the program counter increased by 4.
init R1=4;
init R2=5;

# ADD R1, R2, R3
# The four test data lines below describe the testing of the ADD R1, R2, R3 instruction.
# We first load the machine code into the Databus_in, and then drive the clock to step through the full instruction cycle once.
# Note that the first two columns (in this case) are inputs, meaning they will be set to the provided value.
# The other columns are outputs, which are evaluated after the inputs have been set, and then compared against the given expected values.
# The value 'x' denotes a 'do not care' value. Please click the 'Help' button in this dialog for more information regarding test cases.
0     0x6400123f 0      0   1   x           0          x
1     0x6400123f 0      x   x   x           x          x
0     0          0      1   1   x           x          x
1     0          0      1   1   x           x          9

# Fetch next instruction, check if the program counter increased by 4...
0     0          0      0   1   x           4          x
*/
